// Digital circuit alu.dig as structural Verilog
module alu (
  input  [63:0] A,
  input  [63:0] B,
  input  [2:0] ALUop,
  output [63:0] R
);

  wire [63:0] add_1_s, and_1_out, barrelshifter_1_out, barrelshifter_2_out, div_1_q, mul_1_mul, sub_1_s;

  assign and_1_out = B & A;  // And and_1, 64 bits wide
  Add #(.Bits(64)) add_1 (.a(A), .b(B), .c_i(1'b0), .s(add_1_s));  // open: c_o
  Sub #(.Bits(64)) sub_1 (.a(A), .b(B), .c_i(1'b0), .s(sub_1_s));  // open: c_o
  Mul #(.Bits(32)) mul_1 (.a(A[31:0]), .b(B[31:0]), .mul(mul_1_mul));
  Div #(.Bits(64)) div_1 (.a(A), .b(B), .q(div_1_q));  // open: r
  BarrelShifter #(.Bits(64), .barrelSigned("true")) barrelshifter_1 (.in(A), .shift(B[7:0]), .out(barrelshifter_1_out));
  BarrelShifter #(.Bits(64), .barrelSigned("true"), .direction("right")) barrelshifter_2 (
    .in(A), .shift(B[7:0]), .out(barrelshifter_2_out));
  Multiplexer #(.Selector_Bits(3), .Bits(64)) multiplexer_1 (
    .sel(ALUop), .in_0(add_1_s), .in_1(sub_1_s), .in_2(mul_1_mul), .in_3(div_1_q),
    .in_4(barrelshifter_1_out), .in_5(barrelshifter_2_out), .in_6({A[51:0], {12{1'b0}}}), .in_7(and_1_out),
    .out(R));
endmodule
